// Logisim project 8-1mux-example.circ as structural Verilog: 1 circuit, main circuit main
module main (
  input  in_1,
  input  Cin,
  input  A,
  input  [7:0] in_4,
  input  B,
  input  [7:0] in_6,
  output Sum,
  output [7:0] out_8,
  output Cout,
  output Sum_2,
  output Cout_2
);

  wire adder_2_cout;

  Adder #(.width(1)) adder_1 (.a(A), .b(B), .out(Sum), .cin(Cin), .cout(Cout));
  Multiplexer #(.select(3), .enable("false")) multiplexer_1 (
    .in0(1'b0), .in1(1'b1), .in2(1'b1), .in3(1'b0), .in4(1'b1), .in5(1'b0), .in6(1'b0), .in7(1'b1),
    .out(Sum_2), .sel({Cin, A, B}));
  Multiplexer #(.select(3), .enable("false")) multiplexer_2 (
    .in0(1'b0), .in1(1'b1), .in2(1'b1), .in3(1'b0), .in4(1'b1), .in5(1'b0), .in6(1'b0), .in7(1'b1),
    .out(Cout_2), .sel({Cin, A, B}));
  Adder adder_2 (.a(in_4), .b(in_6), .out(out_8), .cin(in_1), .cout(adder_2_cout));

  // Notes on the sheet:
  //   Select
  //   Select
endmodule
