// Logisim project bf.circ as structural Verilog
module ALU (
  input  [15:0] \input ,
  input  [1:0] opcode,
  output [15:0] \output 
);

  wire [15:0] adder_1_out, subtractor_1_out;

  Adder #(.width(16)) adder_1 (.a(\input ), .b(16'h1), .out(adder_1_out));  // open: cin, cout
  Subtractor #(.width(16)) subtractor_1 (.a(\input ), .b(16'h1), .out(subtractor_1_out));  // open: bin, bout
  Multiplexer #(.select(2), .width(16), .enable("false")) multiplexer_1 (
    .in0(adder_1_out), .in1(subtractor_1_out), .in2(\input ), .out(\output ), .sel(opcode));  // open: in3
endmodule

module RegisterFile (
  input  [15:0] \input ,
  input  write,
  input  [2:0] source,
  input  [2:0] destination,
  output [15:0] \output ,
  output [15:0] PC,
  output [15:0] IR
);

  wire demultiplexer_1_out0, demultiplexer_1_out1, demultiplexer_1_out2, demultiplexer_1_out3,
       demultiplexer_1_out4, demultiplexer_1_out5;
  wire [15:0] data_q, pointer_q, SP_q, Stack_q;

  Demultiplexer #(.select(3), .enable("false")) demultiplexer_1 (
    .out0(demultiplexer_1_out0), .out1(demultiplexer_1_out1), .out2(demultiplexer_1_out2),
    .out3(demultiplexer_1_out3), .out4(demultiplexer_1_out4), .out5(demultiplexer_1_out5), .in(write),
    .sel(destination));  // open: out6, out7
  Register #(.width(16)) pointer (.D(\input ), .Q(pointer_q), .clk(demultiplexer_1_out0));  // open: en, clr
  Register #(.width(16)) data (.D(\input ), .Q(data_q), .clk(demultiplexer_1_out1));  // open: en, clr
  Register #(.width(16)) u_PC (.D(\input ), .Q(PC), .clk(demultiplexer_1_out2));  // open: en, clr
  Register #(.width(16)) u_IR (.D(\input ), .Q(IR), .clk(demultiplexer_1_out3));  // open: en, clr
  Register #(.width(16)) SP (.D(\input ), .Q(SP_q), .clk(demultiplexer_1_out4));  // open: en, clr
  Register #(.width(16)) Stack (.D(\input ), .Q(Stack_q), .clk(demultiplexer_1_out5));  // open: en, clr
  Multiplexer #(.select(3), .width(16), .enable("false")) multiplexer_1 (
    .in0(pointer_q), .in1(data_q), .in2(PC), .in3(IR), .in4(SP_q), .in5(Stack_q), .out(\output ), .sel(source));  // open: in6, in7
endmodule

module Decoder (
  input  [7:0] instruction,
  output [3:0] out_2
);

  ROM #(.dataWidth(4)) rom_1 (.addr(instruction), .data(out_2));  // open: sel

  // Notes on the sheet:
  //   contents of rom_1 (hex, n*v repeats v):
  //   43*0 3 6 4 5 13*0 2 0 1 28*0 7 8
endmodule

module DataPath (
  input  [15:0] \input ,
  input  write,
  input  select,
  input  [2:0] source,
  input  [2:0] dest,
  input  [1:0] opcode,
  output [15:0] \output ,
  output [15:0] PC,
  output [15:0] IR
);

  wire [15:0] multiplexer_1_out, registerfile_1_output;

  Multiplexer #(.width(16), .enable("false")) multiplexer_1 (
    .in0(\output ), .in1(\input ), .out(multiplexer_1_out), .sel(select));
  RegisterFile registerfile_1 (
    .\input (multiplexer_1_out), .write(write), .source(source), .destination(dest),
    .\output (registerfile_1_output), .PC(PC), .IR(IR));
  ALU alu_1 (.\input (registerfile_1_output), .opcode(opcode), .\output (\output ));

  // Notes on the sheet:
  //   Registers
  //   ALU
endmodule

module Stack (
  input  in_1,
  input  [1:0] in_2,
  input  [15:0] data,
  input  write
);

  wire [7:0] bit_extender_2_out, SP_q;
  wire [15:0] alu_1_output, bit_extender_1_out, ram_1_data;

  Register SP (.D(bit_extender_2_out), .Q(SP_q), .clk(in_1));  // open: en, clr
  assign bit_extender_1_out = {{8{1'b0}}, SP_q};  // Bit_Extender bit_extender_1
  ALU alu_1 (.\input (bit_extender_1_out), .opcode(in_2), .\output (alu_1_output));
  Bit_Extender #(.in_width(16), .out_width(8)) bit_extender_2 (.in(alu_1_output), .out(bit_extender_2_out));
  RAM #(.dataWidth(16), .bus("separate")) ram_1 (
    .addr(bit_extender_2_out), .din(data), .data(ram_1_data), .clk(write));  // open: str, sel, ld, clr
endmodule
