// Logisim project bf2.circ as structural Verilog
module ALU (
  input  [15:0] \input ,
  input  [1:0] opcode,
  output [15:0] \output 
);

  wire [15:0] adder_1_out, subtractor_1_out;

  Adder #(.width(16)) adder_1 (.a(\input ), .b(16'h1), .out(adder_1_out));  // open: cin, cout
  Subtractor #(.width(16)) subtractor_1 (.a(\input ), .b(16'h1), .out(subtractor_1_out));  // open: bin, bout
  Multiplexer #(.select(2), .width(16), .enable("false")) multiplexer_1 (
    .in0(adder_1_out), .in1(subtractor_1_out), .out(\output ), .sel(opcode));  // open: in2, in3
endmodule

module RegisterFile (
  input  [15:0] \input ,
  input  write,
  input  [1:0] register,
  output [15:0] \output ,
  output [15:0] PC,
  output [15:0] instruction
);

  wire demultiplexer_1_out0, demultiplexer_1_out1, demultiplexer_1_out2, demultiplexer_1_out3;
  wire [15:0] address_q, data_q;

  Demultiplexer #(.select(2), .enable("false")) demultiplexer_1 (
    .out0(demultiplexer_1_out0), .out1(demultiplexer_1_out1), .out2(demultiplexer_1_out2),
    .out3(demultiplexer_1_out3), .in(write), .sel(register));
  Register #(.width(16)) address (.D(\input ), .Q(address_q), .clk(demultiplexer_1_out0));  // open: en, clr
  Register #(.width(16)) data (.D(\input ), .Q(data_q), .clk(demultiplexer_1_out1));  // open: en, clr
  Register #(.width(16)) u_PC (.D(\input ), .Q(PC), .clk(demultiplexer_1_out2));  // open: en, clr
  Register #(.width(16)) u_instruction (.D(\input ), .Q(instruction), .clk(demultiplexer_1_out3));  // open: en, clr
  Multiplexer #(.select(2), .width(16), .enable("false")) multiplexer_1 (
    .in0(address_q), .in1(data_q), .in2(PC), .in3(instruction), .out(\output ), .sel(register));
endmodule

module Decoder (
  input  [7:0] instruction,
  output [3:0] out_2
);

  ROM #(.dataWidth(4)) rom_1 (.addr(instruction), .data(out_2));  // open: sel

  // Notes on the sheet:
  //   ASCII BF commands
  //   contents of rom_1 (hex, n*v repeats v):
  //   43*0 3 6 4 5 13*0 2 0 1 28*0 7 8
  //   Internal opcode
endmodule

module DataPath (
  input  [15:0] \input ,
  input  source,
  input  write,
  input  [1:0] \reg ,
  input  [3:0] opcode,
  output [15:0] \output ,
  output [15:0] PC,
  output [15:0] instruction
);

  wire [15:0] multiplexer_1_out, registerfile_1_output;

  Multiplexer #(.width(16), .enable("false")) multiplexer_1 (
    .in0(\output ), .in1(\input ), .out(multiplexer_1_out), .sel(source));
  RegisterFile registerfile_1 (
    .\input (multiplexer_1_out), .write(write), .register(\reg ), .\output (registerfile_1_output), .PC(PC),
    .instruction(instruction));
  ALU alu_1 (.\input (registerfile_1_output), .opcode(opcode[1:0]), .\output (\output ));
  // Pins of 2 and 4 bits meet at opcode

  // Notes on the sheet:
  //   Registers
  //   ALU
endmodule

module stack (
  input  [1:0] in_1,
  input  in_2,
  input  [15:0] data,
  input  write
);

  wire [7:0] bit_extender_2_out, SP_q;
  wire [15:0] alu_1_output, bit_extender_1_out, ram_1_data;

  assign bit_extender_1_out = {{8{1'b0}}, SP_q};  // Bit_Extender bit_extender_1
  Register SP (.D(bit_extender_2_out), .Q(SP_q), .clk(in_2));  // open: en, clr
  Bit_Extender #(.in_width(16), .out_width(8)) bit_extender_2 (.in(alu_1_output), .out(bit_extender_2_out));
  ALU alu_1 (.\input (bit_extender_1_out), .opcode(in_1), .\output (alu_1_output));
  RAM #(.dataWidth(16), .bus("separate")) ram_1 (
    .addr(SP_q), .din(data), .data(ram_1_data), .clk(write));  // open: str, sel, ld, clr
endmodule
