// Logisim project gate-intro.circ as structural Verilog: 1 circuit, main circuit main
module main (
  input  x,
  input  y,
  output x_2,
  output x_prime,
  output xy,
  output x_y,
  output xy__prime,
  output x_y__prime,
  output x_y_2,
  output x_y_3
);

  Clock clock_1 ();  // open: out
  buf buffer_1 (x_2, x);
  not \not  (x_prime, x);
  and \and  (xy, x, y);
  or \or  (x_y, x, y);
  nand \nand  (xy__prime, x, y);
  nor \nor  (x_y__prime, x, y);
  xor \xor  (x_y_2, x, y);
  xnor \xnor  (x_y_3, x, y);

  // Notes on the sheet:
  //   Inputs
  //   Some gates
  //   Outputs
endmodule
