// Logisim project logic-expression2.circ as structural Verilog: 3 circuits, main circuit main
module main (
  input  x,
  input  y,
  input  z,
  output x_prime_y_z
);

  wire x_prime_out, y_z_out;

  not x_prime (x_prime_out, x);
  and y_z (y_z_out, y, z);
  or or_1 (x_prime_y_z, x_prime_out, y_z_out);

  // Notes on the sheet:
  //   Inputs
  //   Circuit diagram
  //   Output
endmodule

module majority (
  input  x,
  input  y,
  input  z,
  output majority
);

  wire x_prime_y_z_out, x_y_prime_z_out, x_y_z_out, x_y_z_prime_out;

  and x_prime_y_z (x_prime_y_z_out, ~x, y, z);  // AND_Gate
  and x_y_prime_z (x_y_prime_z_out, x, ~y, z);  // AND_Gate
  and x_y_z_prime (x_y_z_prime_out, x, y, ~z);  // AND_Gate
  and x_y_z (x_y_z_out, x, y, z);
  or or_1 (majority, x_prime_y_z_out, x_y_prime_z_out, x_y_z_prime_out, x_y_z_out);

  // Notes on the sheet:
  //   Inputs
  //   Output
endmodule

module majority_generated (
  input  x,
  input  y,
  input  z,
  output majority
);

  wire and_1_out, and_2_out, and_3_out;

  and and_1 (and_1_out, y, z);
  and and_2 (and_2_out, x, z);
  and and_3 (and_3_out, x, y);
  or or_1 (majority, and_1_out, and_2_out, and_3_out);
endmodule
