// Logisim project memory.circ as structural Verilog: 1 circuit, main circuit main
module main (
  input  s_prime,
  input  r_prime,
  input  in_3,
  input  [7:0] in_4,
  output q,
  output q_prime,
  output out_7,
  output [7:0] out_8
);

  wire clock_1_out;
  wire [7:0] rom_1_data;

  Clock clock_1 (.out(clock_1_out));
  nand nand_1 (q, s_prime, q_prime);
  nand nand_2 (q_prime, q, r_prime);
  Register Register (.D(in_4), .Q(out_8), .clk(clock_1_out));  // open: en, clr
  D_Flip_Flop d_ff_1 (.clk(clock_1_out), .D(in_3), .Q(out_7));  // open: Qn, preset, en, reset
  ROM rom_1 (.addr(in_4), .data(rom_1_data), .sel(1'b1));
  Hex_Digit_Display hex_digit_display_1 (.value(out_8[7:4]));  // open: dp
  // Probe on rom_1_data
  Hex_Digit_Display hex_digit_display_2 (.value(out_8[3:0]));  // open: dp

  // Notes on the sheet:
  //   Wiring -> Clock
  //   (SR)' NAND Latch
  //   Memory -> D flip flop (Delay)
  //   ROM
  //   contents of rom_1 (hex, n*v repeats v):
  //   1 2 3
endmodule
