// Logisim project random-state-machine.circ as structural Verilog: 2 circuits, main circuit main
module main (
  input  \input 
);

  wire clock_1_out;
  wire [2:0] circuit_1_n0, register_1_q;

  circuit circuit_1 (
    .s2(register_1_q[2]), .s1(register_1_q[1]), .s0(register_1_q[0]), .\input (\input ),
    .n2(circuit_1_n0[2]), .n1(circuit_1_n0[1]), .n0(circuit_1_n0[0]));
  Clock clock_1 (.out(clock_1_out));
  Register #(.width(3)) register_1 (.D(circuit_1_n0), .Q(register_1_q), .clk(clock_1_out));  // open: en, clr
  Hex_Digit_Display hex_digit_display_1 (.value({1'b0, register_1_q}));  // open: dp

  // Notes on the sheet:
  //   Wiring -> Pin
  //   State machines are magic
  //   State-transition
  //   Wiring -> Clock
  //   3-bit register
  //   Wiring -> Constant
endmodule

module circuit (
  input  s2,
  input  s1,
  input  s0,
  input  \input ,
  output n2,
  output n1,
  output n0
);

  wire and_1_out, and_2_out, and_3_out, and_4_out, and_5_out, and_6_out, and_7_out, not_1_out, not_2_out,
       not_3_out, not_4_out, not_5_out, not_6_out, not_7_out;

  and and_1 (and_1_out, s1, not_1_out);
  not not_1 (not_1_out, s0);
  and and_2 (and_2_out, s2, not_2_out);
  not not_2 (not_2_out, \input );
  not not_3 (not_3_out, s1);
  and and_3 (and_3_out, not_3_out, s0);
  and and_4 (and_4_out, s0, \input );
  not not_4 (not_4_out, s2);
  and and_5 (and_5_out, not_4_out, not_5_out, not_6_out);
  not not_5 (not_5_out, s1);
  not not_6 (not_6_out, s0);
  not not_7 (not_7_out, s1);
  and and_6 (and_6_out, not_7_out, \input );
  and and_7 (and_7_out, s0, \input );
  or or_1 (n2, and_1_out, and_2_out);
  or or_2 (n1, and_3_out, and_4_out);
  or or_3 (n0, and_5_out, and_6_out, and_7_out);
endmodule
