// Logisim project random.circ as structural Verilog
module random_circuit (
  input  x,
  input  y,
  input  z,
  output f,
  output out
);

  wire and_1_out, and_2_out, not_1_out, not_2_out;

  not not_1 (not_1_out, x);
  not not_2 (not_2_out, y);
  and and_1 (and_1_out, not_1_out, y);
  and and_2 (and_2_out, x, not_2_out, z);
  Multiplexer #(.select(2), .enable("false")) multiplexer_1 (
    .in0(1'b0), .in1(1'b1), .in2(z), .in3(1'b0), .out(out), .sel({x, y}));
  or or_1 (f, and_1_out, and_2_out);

  // Notes on the sheet:
  //   4-1 Multiplexer
endmodule
