// Logisim project random2.circ as structural Verilog
module random (
  input  x,
  input  y,
  input  z,
  output f,
  output mux_f
);

  wire and_1_out, and_2_out, and_3_out, not_1_out, not_2_out, not_3_out, not_4_out, not_5_out;

  not not_1 (not_1_out, x);
  not not_2 (not_2_out, z);
  not not_3 (not_3_out, x);
  not not_4 (not_4_out, y);
  not not_5 (not_5_out, z);
  and and_1 (and_1_out, not_1_out, not_2_out);
  and and_2 (and_2_out, not_3_out, y);
  and and_3 (and_3_out, x, not_4_out, z);
  or or_1 (f, and_1_out, and_2_out, and_3_out);
  Multiplexer #(.select(2), .enable("false")) multiplexer_1 (
    .in0(not_5_out), .in1(1'b1), .in2(z), .in3(1'b0), .out(mux_f), .sel({x, y}));

  // Notes on the sheet:
  //   4-1MUX
endmodule
