// Logisim project vending-machine.circ as structural Verilog: 3 circuits, main circuit main
module main (
  input  reset,
  output [2:0] state
);

  wire bogus_out, clock_out, dime_out, nickel_out, quarter_out;
  wire [1:0] priority_encoder_1_out;
  wire [2:0] rom_1_data;

  Button bogus (.out(bogus_out));
  Button nickel (.out(nickel_out));
  Button dime (.out(dime_out));
  Button quarter (.out(quarter_out));
  Priority_Encoder #(.select(2)) priority_encoder_1 (
    .in0(bogus_out), .in1(nickel_out), .in2(dime_out), .in3(quarter_out), .out(priority_encoder_1_out));  // open: gs, en_out, en_in
  // Probe on priority_encoder_1_out
  ROM #(.addrWidth(5), .dataWidth(3)) rom_1 (.addr({state, priority_encoder_1_out}), .data(rom_1_data));  // open: sel
  Clock clock (.out(clock_out));
  Register #(.width(3)) Register (.D(rom_1_data), .Q(state), .clk(clock_out), .clr(reset));  // open: en

  // Notes on the sheet:
  //   current state
  //   ROM
  //   contents of rom_1 (hex, n*v repeats v):
  //   0 1 2 5 1 2 3 6 2 3 4 6 3 4 5 6 4 5 11*6 1 2 5
  //   next state
endmodule

module vend (
);

  wire undriven;
  wire [2:0] main_1_state;

  main main_1 (.reset(undriven), .state(main_1_state));
endmodule

module vending_machine (
  input  [1:0] \input ,
  input  clock,
  input  reset,
  output [2:0] state
);

  wire [2:0] rom_1_data;

  ROM #(.addrWidth(5), .dataWidth(3)) rom_1 (.addr({state, \input }), .data(rom_1_data));  // open: sel
  Register #(.width(3)) Register (.D(rom_1_data), .Q(state), .clk(clock), .clr(reset));  // open: en

  // Notes on the sheet:
  //   current state
  //   ROM
  //   contents of rom_1 (hex, n*v repeats v):
  //   0 1 2 5 1 2 3 6 2 3 4 6 3 4 5 6 4 5 11*6 1 2 5
  //   next state
endmodule
