// Logisim project xor-as-mux.circ as structural Verilog: 1 circuit, main circuit main
module main (
  input  A,
  input  B,
  output XOR,
  output XOR_2
);

  wire not_1_out;

  not not_1 (not_1_out, B);
  xor xor_1 (XOR, A, B);
  Multiplexer #(.enable("false")) multiplexer_1 (.in0(B), .in1(not_1_out), .out(XOR_2), .sel(A));
endmodule
